# Fritzing sketch Robot Arm V2.1 (saved by Fritzing 0.9.4)

parts:
  LED1 = LED - 3mm [color="Orange (620nm)" package="3 mm [THT]"]
  Part1 = Arduino Nano (Rev3.0)
  BASE = Basic Servo
  LASER_EMMITER = KY-008 Laser Transmitter Module [package="Breakout board"]
  Mod2 = laser receiver [package=THT]
  Part2 = Thumb Joystick
  Part3 = Thumb Joystick
  R2 = Resistor [tolerance=±5% resistance=150 package=THT]
  LS1 = Limit Switch [package="Breakout Board"]
  U1 = SWITCH-SPST-2 [package=switch-spst-vertical]
  FRDR_BUS6 = Module display OLED I2C 128x64 SSD1306 [package=THT]
  5V_POWER1 = Power plug
  part = Electrolytic Capacitor [capacitance=1000μF voltage=10V package="1010 [SMD, electrolytic]"]
  L1 = Basic Servo
  L2 = Basic Servo
  L3 = Basic Servo
  L4 = Basic Servo
  G1 = Basic Servo
  G2 = Basic Servo
  R3 = Resistor [tolerance=±5% resistance=47 package=THT]
  LS2 = Limit Switch [package="Breakout Board"]
  LED2 = LED - 3mm [color="Orange (620nm)" package="3 mm [THT]"]
  LED3 = LED - 3mm [color="Orange (620nm)" package="3 mm [THT]"]
  LED4 = LED - 3mm [color="Orange (620nm)" package="3 mm [THT]"]

nets:
  N1: LED1.cathode, R3.Pin_1, LED2.cathode, LED3.cathode, LED4.cathode
  GND: LED1.anode, Part1.GND, BASE.gnd, LASER_EMMITER.-, Mod2.pin1, Part2.GND, Part3.GND, LS1.G, FRDR_BUS6.GND, 5V_POWER1.GND, part.-, L1.gnd, L2.gnd, L3.gnd, L4.gnd, G1.gnd, G2.gnd, LS2.G, LED2.anode, LED3.anode, LED4.anode
  N2: Part1.D2, BASE.pulse
  N3: Part1.D3, L1.pulse
  N4: Part1.D4, L2.pulse
  N5: Part1.D5, L3.pulse
  N6: Part1.D6, L4.pulse
  N7: Part1.D7, G1.pulse
  N8: Part1.D8, G2.pulse
  N9: Part1.D9, R2.Pin_1
  N10: Part1.D10, R3.Pin_0
  N11: Part1.D11/MOSI, LS1.S
  N12: Part1.D12/MISO, LS2.S
  VCC: Part1.VIN, BASE.vcc, U1.P, part.+, L1.vcc, L2.vcc, L3.vcc, L4.vcc, G1.vcc, G2.vcc
  VCC_2: Part1.5V, Mod2.pin3, Part2.VCC, Part3.VCC, FRDR_BUS6.VCC
  N13: Part1.A6, Mod2.pin2
  N14: Part1.A5, FRDR_BUS6.SCL
  N15: Part1.A4, FRDR_BUS6.SDA
  N16: Part1.A3, Part2.HORZ
  N17: Part1.A2, Part3.VERT
  N18: Part1.A1, Part3.SEL
  N19: Part1.A0, Part3.HORZ
  N20: LASER_EMMITER.S, R2.Pin_0
  N21: U1.O, 5V_POWER1.VCC

notes:
  Robot Arm, 4

custom parts:
  KY-008 Laser Transmitter Module: KY-008 Laser Transmitter Module, emits a dot shaped red laser beam.
  laser receiver: Generic non modulated laser receiver module.
  Limit Switch: Generic limit switch commonly found on 3D printers. Typical lever microswitch mounted on a PCB board with a 3 pin JST XH connector.
  Module display OLED I2C 128x64 SSD1306: Ecran OLED I2C SSD163 de 128x64 avec connexion I2C
